// Logisim project 2 bit signed comparator.circ as structural Verilog: 1 circuit, main circuit main
module main (
  input  [1:0] a,
  input  [1:0] b,
  output c
);

  wire and_1_out, and_2_out, and_3_out, not_1_out, not_2_out, not_3_out, not_4_out;

  not not_1 (not_1_out, a[1]);
  not not_2 (not_2_out, a[1]);
  not not_3 (not_3_out, b[0]);
  not not_4 (not_4_out, b[0]);
  and and_1 (and_1_out, not_1_out, b[1]);
  or or_1 (c, and_1_out, and_2_out, and_3_out);
  and and_2 (and_2_out, not_2_out, a[0], not_3_out);
  and and_3 (and_3_out, a[0], b[1], not_4_out);
endmodule
